# Fritzing sketch CansatBasico (saved by Fritzing 0.9.3b)
breadboards: 1

parts:
  Componente1 = APC220 with antenna
  Componente2 = Barometric Pressure Sensor - BMP180 Breakout (GY-68)
  Componente3 = Arduino Uno (Rev3)
  Componente4 = u-blox NEO-6M GPS Breakout
  VCC1 = Battery
  S1 = Toggle Switch [package=THT]

nets:
  GND: Componente1.GND, Componente2.GND, Componente3.GND, Componente4.GND, S1.COM
  VCC: Componente1.VCC, Componente2.VCC, Componente3.3V3, Componente4.VCC
  N1: Componente1.EN, Componente1.SET
  N2: Componente1.RXD, Componente3.D7
  N3: Componente2.SCL, Componente3.A5/SCL
  N4: Componente2.SDA, Componente3.A4/SDA
  N5: Componente3.D4, Componente4.TXD
  N6: Componente3.VIN, VCC1.+
  N7: VCC1.-, S1.L1

custom parts:
  APC220 with antenna: Radio transceiver module for Arduino operating in the 418-455MHz band.
